# Fritzing sketch FRITZING_ESQUEMA (saved by Fritzing 0.9.10b)
circuit board: 8.46667cm x 5.64444cm
breadboards: 1

parts:
  KY-1 = Keyes Relay [package=THT]
  KY-2 = Keyes Relay [package=THT]
  Componente1 = Arduino Uno (Rev3)
  S1 = Pushbutton [package="[THT]"]
  S2 = Pushbutton [package="[THT]"]
  R1 = Photocell (LDR) [package=THT]
  R2 = Resistor [tolerance=±5% power=0.25 resistance=220 package=THT]

nets:
  N1: KY-1.signal, Componente1.D7
  N2: KY-1.power, KY-2.power, Componente1.5V, R1.pin_0
  N3: KY-1.ground, KY-2.ground, Componente1.GND, S1.Pin_1, S1.Pin_2, S2.Pin_1, S2.Pin_2, R2.Pin_0
  N4: KY-2.signal, Componente1.D6_PWM
  N5: KY-2.NC, KY-2.C, KY-2.NO
  N6: Componente1.A0, R1.pin_1, R2.Pin_1
  N7: Componente1.D4, S2.Pin_3, S2.Pin_4
  N8: Componente1.D5_PWM, S1.Pin_3, S1.Pin_4

custom parts:
  Keyes Relay: The Keyes 5V relay module is suitable for SCM development, home appliance control. It uses a 5V~12V TIL control signal which can control DC / AC signal.
